# Fritzing sketch PiKiosk (saved by Fritzing 0.9.2b)

parts:
  Raspberry_Pi1 = Raspberry Pi 2
  Part2 = Bluetooth HC-05 Macho

nets:
  N1: Raspberry_Pi1.GPIO15, Part2.TXD
  N2: Raspberry_Pi1.GPIO14, Part2.RXD
  GND: Raspberry_Pi1.GND, Part2.GND
  5V: Raspberry_Pi1.5V, Part2.VCC

notes:
  If your hc05 have inbuilt regulator then connect it to 5v supply otherwise use 3v3 supply
