# Fritzing sketch TemperatureContoller (saved by Fritzing 0.9.2b)

parts:
  Part1 = Arduino Uno (Rev3) - ICSP
  Raspberry_Pi1 = Raspberry Pi 2
  Part2 = Logic Level Converter
  T1 = LM35 Temperature Sensor [package="TO92 [THT]"]

nets:
  N1: Part1.A0, T1.Vout
  GND: Part1.GND, Raspberry_Pi1.GND, Part2.GND
  N2: Part1.D2, Part2.TX2_HV
  N3: Part1.D3_PWM, Part2.RX2_HV
  N4: Part1.5V, Part2.HV
  N5: Raspberry_Pi1.GPIO15, Part2.RX2_LV
  N6: Raspberry_Pi1.GPIO14, Part2.TX2_LV
